# Fritzing sketch Embedded mid-term_14 (saved by Fritzing 0.9.10b)

parts:
  U1 = ESP32-38PinWide [part_number=ESP32-38PinWide]
  VCC1 = 4 x AAA Battery Mount
  U2 = GAS_SENSOR [package=mq-3]
  M1 = Dagu DGServo 9g (Pan and tilt) [part_number=RS001B]
  R1 = Resistor [tolerance=±5% power=0.25 resistance=330 package=THT]
  SG1 = Buzzer 12mm [package=buzzer-ccv-kit]
  S1 = Pushbutton [package="[THT]"]
  S2 = Pushbutton [package="[THT]"]
  LED1 = LED - 5mm [color="Yellow (595nm)" current=0.030 package="5 mm [THT]"]
  LED2 = LED - 5mm [color="Red (633nm)" current=0.030 package="5 mm [THT]"]
  R2 = Resistor [tolerance=±5% power=0.25 resistance=220 package=THT]
  R3 = Resistor [tolerance=±5% power=0.25 resistance=220 package=THT]
  Grove1 = Grove OLED 128x96
  DI1 = 7 Segment Display
  R4 = Resistor [tolerance=±5% power=0.25 resistance=220 package=THT]
  R5 = Resistor [tolerance=±5% power=0.25 resistance=220 package=THT]
  R6 = Resistor [tolerance=±5% power=0.25 resistance=220 package=THT]
  R7 = Resistor [tolerance=±5% power=0.25 resistance=220 package=THT]
  R8 = Resistor [tolerance=±5% power=0.25 resistance=220 package=THT]
  R9 = Resistor [tolerance=±5% power=0.25 resistance=220 package=THT]
  R10 = Resistor [tolerance=±5% power=0.25 resistance=220 package=THT]
  R11 = Resistor [tolerance=±5% power=0.25 resistance=220 package=THT]

nets:
  N1: U1.GPIO36, R1.Pin_1
  N2: U1.GPIO33, M1.pulse
  N3: U1.GPIO27, SG1.1
  GND: U1.GPIO14, U1.GPIO12, U1.GND, VCC1.-, U2.H2, M1.gnd, SG1.2, S1.Pin_1, S1.Pin_2, S2.Pin_1, S2.Pin_2, LED1.cathode, LED2.cathode
  VCC: U1.VIN, VCC1.+, U2.H1, M1.vcc, Grove1.VCC
  N4: U1.GPIO15, R3.Pin_0
  N5: U1.GPIO2, R2.Pin_0
  N6: U1.GPIO0, R4.Pin_0
  N7: U1.GPIO4, R8.Pin_0
  N8: U1.GPIO16, R9.Pin_0
  N9: U1.GPIO17, R11.Pin_0
  N10: U1.GPIO5, R10.Pin_0
  N11: U1.GPIO18, R5.Pin_0
  N12: U1.GPIO19, R6.Pin_0
  N13: U1.GPIO21, Grove1.SCL
  N14: U1.GPIO22, Grove1.SDA
  N15: U2.A1, R1.Pin_0
  N16: LED1.anode, R3.Pin_1
  N17: LED2.anode, R2.Pin_1
  N18: DI1.Segment_A#1, R6.Pin_1
  N19: DI1.Segment_F, R5.Pin_1
  N20: DI1.Segment_E, R10.Pin_1
  N21: DI1.Segment_D, R11.Pin_1
  N22: DI1.Segment_DP, R7.Pin_1
  N23: DI1.Segment_C, R9.Pin_1
  N24: DI1.Segment_B, R8.Pin_1
  N25: DI1.Segment_A#10, R4.Pin_1

custom parts:
  ESP32-38PinWide: Generic 38-Pin ESP32 with wide format (only access to one side of pins on a breadboard) based on Stephen Lilley's HiLetgo ESP-WROOM-32 ESP32 ESP-32S Development Board.
